# Fritzing sketch DispenserFritzing (saved by Fritzing 0.9.4)
breadboards: 2

parts:
  Teensy_3_1 = Teensy 3.1
  WIZ820io1 = WIZ820io [part_number=WIZ820io]
  SP1 = SPEAKER [package=pcb_mount_speaker]
  J1 = Basic Servo
  Part1 = 12 NeoPixel Ring [part_number=1643]
  OLED_I2C1 = OLED 128x64 I2C Monochrome Display
  Part2 = HC-SR501 Body Sensor Module
  M2 = BMP280
  Part3 = 4x4 Keypad [part_number=101207]

nets:
  GND: Teensy_3_1.GND, SP1.+, J1.gnd, Part1.GND, OLED_I2C1.GND, Part2.GND, M2.GND
  N1: Teensy_3_1.D2, Part3.8
  N2: Teensy_3_1.D3, Part3.7
  N3: Teensy_3_1.D4, Part3.6
  N4: Teensy_3_1.D5, Part3.5
  N5: Teensy_3_1.D6, Part3.4
  N6: Teensy_3_1.D7, Part3.3
  N7: Teensy_3_1.D8, Part3.2
  N8: Teensy_3_1.D9, WIZ820io1.nRESET, Part3.1
  N9: Teensy_3_1.D11, WIZ820io1.MOSI
  N10: Teensy_3_1.D12, WIZ820io1.nSS, WIZ820io1.MISO
  N11: Teensy_3_1.D13, WIZ820io1.SCLK
  N12: Teensy_3_1.A0/D14, SP1.-
  N13: Teensy_3_1.A4/D18, OLED_I2C1.SDA, M2.SDA
  N14: Teensy_3_1.A5/D19, OLED_I2C1.SCK, M2.SCL
  N15: Teensy_3_1.A7/D21, Part2.OUT
  N16: Teensy_3_1.A8/D22, J1.pulse
  N17: Teensy_3_1.A9/D23, Part1.IN
  VIN: Teensy_3_1.3V3, WIZ820io1.VIN, J1.vcc, OLED_I2C1.VDD, Part2.VCC, M2.VIN
  VIN_2: Teensy_3_1.Vin, Part1.VDD

custom parts:
  12 NeoPixel Ring: 12 ultra bright smart LED NeoPixels are arranged in a circle with 1.5" (37mm) outer diameter. The rings are 'chainable' - connect the output pin of one to the input pin of another. Use only one microcontroller pin to control as many as you can chain together! Each LED is addressable as the driver chip is inside the LED. Each one has ~18mA constant current drive so the color will be very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
  HC-SR501 Body Sensor Module: Pyroelectric Infrared PIR Motion Sensor Detector Module
  BMP280: Temperature Humidity Barometric presure Sensor, I2C
  4x4 Keypad: Matrix membrane keypad 4x4
